# Fritzing sketch Project1_Sketch (saved by Fritzing 0.9.3b)
breadboards: 1

parts:
  Part1 = Photon
  J1 = Infrared Proximity Sensor
  J2 = Infrared Proximity Sensor
  R1 = Resistor [tolerance=±5% resistance=220 package=THT]
  R2 = Resistor [tolerance=±5% resistance=220 package=THT]  # not connected

nets:
  N1: Part1.A0, J1.Vout
  N2: Part1.A1, J2.Vout
  GND: Part1.GND, J1.GND, J2.GND
  VCC: Part1.3V3, J1.Vcc, J2.Vcc
  N3: R1.Pin_0, R1.Pin_1
